# Fritzing sketch laser control synap.sys (saved by Fritzing 0.8.7b)
circuit board: 10.16cm x 5.36194cm
circuit board: 1cm x 1cm
breadboards: 1

parts:
  J1 = Basic Servo
  J2 = Basic Servo
  Power_plug1 = Power plug
  J3 = Basic Servo
  J4 = Basic Servo
  J5 = male pin header, 3 pins [form="♂ (male)"]
  U1 = Voltage Regulator - 5V [package="TO220 [THT]"]
  J6 = male pin header, 3 pins [form="♂ (male)"]
  J7 = male pin header, 3 pins [form="♂ (male)"]
  J8 = male pin header, 3 pins [form="♂ (male)"]
  R1 = Resistor [tolerance=±5% resistance=5k package=THT]
  R2 = Resistor [tolerance=±5% resistance=5k package=THT]
  R3 = Resistor [tolerance=±5% resistance=5k package=THT]
  J9 = Basic Servo
  J10 = male pin header, 3 pins [form="♂ (male)"]
  R5 = Resistor [tolerance=±5% resistance=5k package=THT]
  U3 = Voltage Regulator - Variable [package="TO220 [THT]"]
  C1 = Ceramic Capacitor [capacitance=100nF package="100 mil [THT, multilayer]"]
  C2 = Ceramic Capacitor [capacitance=100nF package="100 mil [THT, multilayer]"]
  C3 = Ceramic Capacitor [capacitance=100nF package="100 mil [THT, multilayer]"]
  R6 = Resistor [tolerance=±5% resistance=240 package=THT]
  R7 = Resistor [tolerance=±5% resistance=330 package=THT]
  R8 = Resistor [tolerance=±5% resistance=5k package=THT]
  R9 = Resistor [tolerance=±5% resistance=330k package=THT]
  R10 = Resistor [tolerance=±5% resistance=330k package=THT]
  R11 = Resistor [tolerance=±5% resistance=330k package=THT]
  R12 = Resistor [tolerance=±5% resistance=330k package=THT]
  R13 = Resistor [tolerance=±5% resistance=330k package=THT]
  Q6 = Basic FET N-Channel [package="TO220 [THT]"]
  Q7 = Basic FET N-Channel [package="TO220 [THT]"]
  Q8 = Basic FET N-Channel [package="TO220 [THT]"]
  Q9 = Basic FET N-Channel [package="TO220 [THT]"]
  Q10 = Basic FET N-Channel [package="TO220 [THT]"]
  D1 = Rectifier Diode [part_number=1N4001 package="300 mil [THT]"]
  R14 = Resistor [tolerance=±5% resistance=90 package=THT]
  LED1 = LED - 3mm [color="Red (633nm)" package="3 mm [THT]"]
  R15 = Resistor [tolerance=±5% resistance=90 package=THT]
  LED2 = LED - 3mm [color="Red (633nm)" package="3 mm [THT]"]
  J11 = female pin header, 3 pins [form="♀ (female)"]
  R16 = Resistor [tolerance=±5% resistance=2k package=THT]
  SW1 = DIP SWITCH [package=dipswitch-02]
  R17 = Resistor [tolerance=±5% resistance=5.6k package=THT]
  R18 = Temperature Sensor (Thermistor) [thermistor_type=NTC package=THT]
  R19 = Resistor [tolerance=±5% resistance=10k package=THT]
  R20 = Temperature Sensor (Thermistor) [thermistor_type=NTC package=THT]
  R21 = Resistor [tolerance=±5% resistance=10k package=THT]
  U4 = Voltage Regulator - Variable [package="TO220 [THT]"]
  R22 = Resistor [tolerance=±5% resistance=3 power=1W package=THT]
  R23 = Resistor [tolerance=±5% resistance=3 package=THT]
  Q11 = NPN-Transistor [package="TO92 [THT]"]
  R24 = Resistor [tolerance=±5% resistance=1.5 power=0.5W package=THT]
  Q12 = NPN-Transistor [package="TO92 [THT]"]
  R25 = Resistor [tolerance=±5% resistance=1.5 power=0.5W package=THT]
  Componente1 = Arduino Mega 2560 (Rev3)
  Q13 = NPN-Transistor [package="TO92 [THT]"]
  R26 = Resistor [tolerance=±5% resistance=1.5 power=0.5W package=THT]
  R27 = Resistor [tolerance=±5% resistance=1.5 power=0.5W package=THT]
  R28 = Resistor [tolerance=±5% resistance=1.5 power=0.5W package=THT]
  Q14 = NPN-Transistor [package="TO92 [THT]"]
  Q15 = NPN-Transistor [package="TO92 [THT]"]

nets:
  GND/GND_LASER/GND_Servo: J1.gnd, J2.gnd, Power_plug1.GND, J3.gnd, J4.gnd, J5.pin2, U1.GND, J6.pin2, J7.pin2, J8.pin2, J9.gnd, J10.pin2, C1.0, C2.1, C3.1, R7.Pin_0, R9.Pin_0, R10.Pin_0, R11.Pin_0, R12.Pin_0, R13.Pin_0, LED1.cathode, LED2.cathode, J11.pin2, R19.Pin_0, R21.Pin_0, Q11.E, R24.Pin_0, Q12.E, R25.Pin_0, Componente1.GND, Q13.E, R26.Pin_0, R27.Pin_0, Q15.E
  5V_-_Servos: J1.vcc, J2.vcc, J3.vcc, J4.vcc, U1.output_voltage, J9.vcc, C1.1
  Signal_2_Servo: J1.pulse, Componente1.D8_PWM
  Signal_1_Servo: J2.pulse, Componente1.D7_PWM
  N1: Power_plug1.VCC, D1.anode
  Signal_3_Servo: J3.pulse, Componente1.D10_PWM
  Signal_4_Servo: J4.pulse, Componente1.D11_PWM
  3.3V_Laser: J5.pin1, J6.pin1, J7.pin1, J8.pin1, J10.pin1, C2.0, R6.Pin_1, R15.Pin_0, J11.pin1, R16.Pin_1, R17.Pin_1, R22.Pin_1, R23.Pin_1
  Sinal_out_5_laser: J5.pin3, Q6.drain, J11.pin3
  N2: U1.input_voltage, U3.IN, C3.0, D1.cathode, U4.IN
  N3: J6.pin3, Q7.drain
  N4: J7.pin3, Q8.drain
  N5: J8.pin3, Q9.drain
  N6: R1.Pin_0, R9.Pin_1, Q9.gate, Q14.C
  Sinal_1_Laser: R1.Pin_1, Componente1.D4_PWM
  N7: R2.Pin_0, R10.Pin_1, Q8.gate, Q13.C
  Sinal_4_Laser: R2.Pin_1, Componente1.D5_PWM
  N8: R3.Pin_0, R11.Pin_1, Q7.gate, Q12.C
  Sinal_5_Laser: R3.Pin_1, R14.Pin_0, Componente1.D6_PWM
  Signal_5_Servo: J9.pulse, Componente1.D12_PWM
  N9: J10.pin3, Q10.drain
  N10: R5.Pin_0, R13.Pin_1, Q10.gate, Q15.C
  Sinal_2_Laser: R5.Pin_1, Componente1.D3_PWM
  N11: U3.ADJ, R6.Pin_0, R7.Pin_1, SW1.3, SW1.4, U4.ADJ
  N12: U3.OUT, R22.Pin_0
  N13: R8.Pin_0, R12.Pin_1, Q6.gate, Q11.C
  Sinal_3_Laser: R8.Pin_1, Componente1.D2_PWM
  N14: Q6.source, Q11.B, R24.Pin_1
  N15: Q7.source, Q12.B, R25.Pin_1
  N16: Q8.source, Q13.B, R26.Pin_1
  N17: Q9.source, Q14.B
  N18: Q10.source, R28.Pin_1, Q15.B
  N19: R14.Pin_1, LED1.anode
  N20: R15.Pin_1, LED2.anode
  N21: R16.Pin_0, SW1.2
  N22: SW1.1, R17.Pin_0
  Termo Sensor Laser: R18.pin_0, R19.Pin_1, Componente1.A0
  5V: R18.pin_1, R20.pin_1, Componente1.5V
  Termo Sensor Servo: R20.pin_0, R21.Pin_1, Componente1.A1
  N23: U4.OUT, R23.Pin_0
  sinal_ventilacao: Componente1.D9_PWM
  N24: R27.Pin_1, Q14.E
