# Fritzing sketch synap.sys (saved by Fritzing 0.8.7b)
circuit board: 10.16cm x 5.36194cm
breadboards: 1

parts:
  R1 = Resistor [tolerance=±5% resistance=10k package=THT]
  R2 = Resistor [tolerance=±5% resistance=10k package=THT]
  R3 = Resistor [tolerance=±5% resistance=10k package=THT]
  R4 = Resistor [tolerance=±5% resistance=10k package=THT]
  R5 = Resistor [tolerance=±5% resistance=10k package=THT]
  R6 = Resistor [tolerance=±5% resistance=10k package=THT]
  R7 = Resistor [tolerance=±5% resistance=10k package=THT]
  R8 = Resistor [tolerance=±5% resistance=10k package=THT]
  Componente1 = Arduino Mega 2560 (Rev3)
  J1 = male pin header, 29 pins [form="♂ (male)"]
  R9 = Resistor [tolerance=±5% resistance=10k package=THT]
  R10 = Resistor [tolerance=±5% resistance=10k package=THT]
  R11 = Resistor [tolerance=±5% resistance=10k package=THT]
  R12 = Resistor [tolerance=±5% resistance=10k package=THT]
  R13 = Resistor [tolerance=±5% resistance=10k package=THT]
  R14 = Resistor [tolerance=±5% resistance=10k package=THT]
  R15 = Resistor [tolerance=±5% resistance=10k package=THT]
  R16 = Resistor [tolerance=±5% resistance=10k package=THT]
  R17 = Resistor [tolerance=±5% resistance=10k package=THT]
  R18 = Resistor [tolerance=±5% resistance=10k package=THT]
  R19 = Resistor [tolerance=±5% resistance=10k package=THT]
  R20 = Resistor [tolerance=±5% resistance=10k package=THT]
  R21 = Resistor [tolerance=±5% resistance=10k package=THT]
  R22 = Resistor [tolerance=±5% resistance=10k package=THT]
  R23 = Resistor [tolerance=±5% resistance=10k package=THT]
  R24 = Resistor [tolerance=±5% resistance=10k package=THT]
  R26 = Resistor [tolerance=±5% resistance=10k package=THT]
  R27 = Resistor [tolerance=±5% resistance=10k package=THT]
  R28 = Resistor [tolerance=±5% resistance=10k package=THT]
  R29 = Resistor [tolerance=±5% resistance=10k package=THT]
  R30 = Resistor [tolerance=±5% resistance=10k package=THT]
  R31 = Resistor [tolerance=±5% resistance=10k package=THT]
  R32 = Resistor [tolerance=±5% resistance=10k package=THT]
  R33 = Resistor [tolerance=±5% resistance=10k package=THT]
  R34 = Rotary Potentiometer (Small) [maximum_resistance=100kΩ package=THT]
  R35 = Rotary Potentiometer (Small) [maximum_resistance=100kΩ package=THT]
  R36 = Rotary Potentiometer (Small) [maximum_resistance=100kΩ package=THT]
  R37 = Rotary Potentiometer (Small) [maximum_resistance=100kΩ package=THT]

nets:
  GND: R1.Pin_0, R2.Pin_0, R3.Pin_0, R4.Pin_0, R5.Pin_0, R6.Pin_0, R7.Pin_0, R8.Pin_0, Componente1.GND, R9.Pin_0, R10.Pin_0, R11.Pin_0, R12.Pin_0, R13.Pin_0, R14.Pin_0, R15.Pin_0, R16.Pin_0, R17.Pin_1, R18.Pin_1, R19.Pin_1, R20.Pin_1, R21.Pin_1, R22.Pin_1, R23.Pin_1, R24.Pin_1, R26.Pin_1, R27.Pin_1, R28.Pin_1, R29.Pin_1, R30.Pin_1, R31.Pin_1, R32.Pin_1, R33.Pin_1, R34.leg2, R35.leg2, R36.leg2, R37.leg2
  N1: R1.Pin_1, Componente1.D12_PWM, J1.pin1
  N2: R2.Pin_1, Componente1.D11_PWM, J1.pin2
  N3: R3.Pin_1, Componente1.D10_PWM, J1.pin3
  N4: R4.Pin_1, Componente1.D9_PWM, J1.pin4
  N5: R5.Pin_1, Componente1.D8_PWM, J1.pin5
  N6: R6.Pin_1, Componente1.D7_PWM, J1.pin6
  N7: R7.Pin_1, Componente1.D6_PWM, J1.pin7
  N8: R8.Pin_1, Componente1.D5_PWM, J1.pin8
  N9: Componente1.A8, R36.wiper
  N10: Componente1.A12, R35.wiper
  N11: Componente1.A0, R34.wiper
  N12: Componente1.A4, R37.wiper
  N13: Componente1.D19/RX1, J1.pin17, R23.Pin_0
  N14: Componente1.D18/TX1, J1.pin16, R32.Pin_0
  N15: Componente1.D17_PWM/RX2, J1.pin15, R9.Pin_1
  N16: Componente1.D16_PWM/TX2, J1.pin14, R10.Pin_1
  N17: Componente1.D15/RX3, J1.pin13, R11.Pin_1
  N18: Componente1.D14/TX3, J1.pin12, R13.Pin_1
  5V: Componente1.5V, R34.leg1, R35.leg1, R36.leg1, R37.leg1
  N19: Componente1.D2_PWM, J1.pin11, R14.Pin_1
  N20: Componente1.D3_PWM, J1.pin10, R15.Pin_1
  N21: Componente1.D4_PWM, J1.pin9, R16.Pin_1
  N22: Componente1.D22, J1.pin18, R22.Pin_0
  N23: Componente1.D24, J1.pin19, R28.Pin_0
  N24: Componente1.D26, J1.pin20, R29.Pin_0
  N25: Componente1.D28, J1.pin21, R30.Pin_0
  N26: Componente1.D30, J1.pin22, R31.Pin_0
  N27: Componente1.D32, J1.pin23, R24.Pin_0
  N28: Componente1.D34, J1.pin24, R26.Pin_0
  N29: Componente1.D44, J1.pin29, R17.Pin_0
  N30: Componente1.D46, J1.pin28, R18.Pin_0
  N31: Componente1.D48, J1.pin27, R19.Pin_0
  N32: Componente1.D50, J1.pin26, R20.Pin_0
  N33: Componente1.D52, J1.pin25, R21.Pin_0
